# Fritzing sketch controller (saved by Fritzing 0.9.3b)
circuit board: 12cm x 5.5cm
breadboards: 1

parts:
  DEC_- = Pushbutton [part_number=btnDown package="[THT]"]
  RA_- = Pushbutton [part_number=btnLeft package="[THT]"]
  Motor_PWR = 2.1mm Barrel Jack with Terminal Block
  R1 = Resistor [tolerance=±5% resistance=220 package=THT]
  LED2 = LED - 3mm [color="Red (633nm)" part_number=ledLeft package="3 mm [THT]"]
  R2 = Resistor [tolerance=±5% resistance=220 package=THT]
  R3 = Resistor [tolerance=±5% resistance=220 package=THT]
  LED4 = LED - 3mm [color="Red (633nm)" part_number=ledDown package="3 mm [THT]"]
  R4 = Resistor [tolerance=±5% resistance=220 package=THT]
  Feather_M4_Express = Adafruit Feather M4 Express [part_number="Adafruit #3857"]
  DC_Stepper_Wing = Adafruit DC+Stepper FeatherWing [part_number="Adafruit #2927"]
  LED3 = LED - 3mm [color="Red (633nm)" part_number=ledUp package="3 mm [THT]"]
  LED1 = LED - 3mm [color="Red (633nm)" part_number=ledRight package="3 mm [THT]"]
  RA_+ = Pushbutton [part_number=btnRight package="[THT]"]
  DEC_+ = Pushbutton [part_number=btnUp package="[THT]"]

nets:
  GND: DEC_-.Pin_1, DEC_-.Pin_2, RA_-.Pin_1, RA_-.Pin_2, Motor_PWR.NEG, R1.Pin_0, R2.Pin_0, R3.Pin_0, R4.Pin_0, Feather_M4_Express.GND, DC_Stepper_Wing.GND, RA_+.Pin_1, RA_+.Pin_2, DEC_+.Pin_1, DEC_+.Pin_2
  N1: DEC_-.Pin_3, DEC_-.Pin_4, Feather_M4_Express.D4
  N2: RA_-.Pin_3, RA_-.Pin_4, Feather_M4_Express.D6
  N3: Motor_PWR.POS, DC_Stepper_Wing.VMOTOR
  N4: R1.Pin_1, LED1.cathode
  N5: LED2.cathode, R2.Pin_1
  N6: LED2.anode, Feather_M4_Express.A4
  N7: R3.Pin_1, LED3.cathode
  N8: LED4.cathode, R4.Pin_1
  N9: LED4.anode, Feather_M4_Express.A2
  N10: Feather_M4_Express.A5, LED1.anode
  N11: Feather_M4_Express.A3, LED3.anode
  +3V3: Feather_M4_Express.+3V3, DC_Stepper_Wing.+3.3V
  N12: Feather_M4_Express.D9, RA_+.Pin_3, RA_+.Pin_4
  N13: Feather_M4_Express.D5, DEC_+.Pin_3, DEC_+.Pin_4
  N14: Feather_M4_Express.SCL, DC_Stepper_Wing.SCL
  N15: Feather_M4_Express.SDA, DC_Stepper_Wing.SDA

notes:
  Telescope Controller, Simple stepper motor controller curcuit suitable for use with a basic telescope motor drive., 1.0

custom parts:
  Adafruit Feather M4 Express: It's what you've been waiting for, the Feather M4 Express featuring ATSAMD51. This Feather is fast like a swift, smart like an owl, strong like a ox-bird (it's half ox, half bird, OK?) This feather is powered by our new favorite chip, the ATSAMD51J19 - with its 120MHz Cortex M4 with floating point support and 512KB Flash and 192KB RAM. Your code will zig and zag and zoom, and with a bunch of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
  Adafruit DC+Stepper FeatherWing: This is the DC Motor + Stepper FeatherWing which will let you use 2 x bi-polar stepper motors or 4 x brushed DC motorx (or 1 stepper and 2 DC motors). Using our Feather Stacking Headers or Feather Female Headers you can connect a FeatherWing on top or bottom of your Feather board and let the board take flight! The original Adafruit Motorshield Kit is one of our most beloved kits, which is why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
